# Fritzing sketch MakerVisitFinalAnode (saved by Fritzing 0.8.5b)
breadboards: 1

parts:
  Part2 = Arduino Uno (Rev3)
  U1 = 74HC595 [package="DIP16 [THT]"]
  LED1 = LED - 5mm [color="Red (633nm)" package="5 mm [THT]"]
  R1 = Resistor [tolerance=±5% resistance=220 package=THT]
  R3 = Resistor [tolerance=±5% resistance=220 package=THT]
  R5 = Resistor [tolerance=±5% resistance=220 package=THT]
  R6 = Resistor [tolerance=±5% resistance=220 package=THT]
  R8 = Resistor [tolerance=±5% resistance=220 package=THT]
  R9 = Resistor [tolerance=±5% resistance=220 package=THT]
  R10 = Resistor [tolerance=±5% resistance=220 package=THT]
  U2 = 7-SEGMENT-DISPLAY [package=7-segment-display]
  R11 = Resistor [tolerance=±5% resistance=220 package=THT]
  R4 = Resistor [tolerance=±5% resistance=220 package=THT]

nets:
  N1: Part2.D8, U1.DS
  N2: Part2.D9_PWM, U1.OE
  N3: Part2.D10_PWM/SS, U1.ST_CP
  N4: Part2.D11_PWM/MOSI, U1.SH_CP
  N5: Part2.D12/MISO, U1.MR
  5V: Part2.5V, U1.VCC
  N6: Part2.GND, LED1.cathode, U2.C
  N7: U1.Q1, R8.Pin_1
  N8: U1.Q2, R3.Pin_1
  N9: U1.Q3, R6.Pin_1
  N10: U1.Q4, R4.Pin_1
  N11: U1.Q5, R5.Pin_1
  N12: U1.Q6, R1.Pin_1
  N13: U1.Q7, R11.Pin_1
  N14: U1.GND, U2.F
  N15: U1.Q7', R10.Pin_0
  N16: U1.Q0, R9.Pin_1
  N17: LED1.anode, R10.Pin_1
  N18: R1.Pin_0, U2.G
  N19: R3.Pin_0, U2.G1
  N20: R5.Pin_0, U2.G2
  N21: R6.Pin_0, U2.D
  N22: R8.Pin_0, U2.DP
  N23: R9.Pin_0, U2.B
  N24: U2.E, R11.Pin_0
  N25: U2.A, R4.Pin_0
